// Logisim project branch-comp.circ as structural Verilog: 1 circuit, main circuit branch_comp
module branch_comp (
  input  [31:0] BrData1,
  input  [31:0] BrData2,
  input  BrUn,
  output BrEq,
  output BrLt
);

  wire comparator_1_eq, comparator_1_lt, comparator_2_eq, comparator_2_lt, not_1_out;

  Comparator #(.mode("unsigned"), .width(32)) comparator_1 (
    .a(BrData1), .b(BrData2), .eq(comparator_1_eq), .lt(comparator_1_lt));  // open: gt
  Comparator #(.width(32)) comparator_2 (
    .a(BrData1), .b(BrData2), .eq(comparator_2_eq), .lt(comparator_2_lt));  // open: gt
  not not_1 (not_1_out, BrUn);
  Multiplexer multiplexer_1 (.in0(comparator_1_lt), .in1(comparator_2_lt), .out(BrLt), .sel(not_1_out));
  Multiplexer multiplexer_2 (.in0(comparator_1_eq), .in1(comparator_2_eq), .out(BrEq), .sel(not_1_out));

  // Notes on the sheet:
  //   INPUTS to your circuit
  //   Unsigned
  //   2-complements/Signed
  //   DON'T CHANGE THE LOCATIONS OF THE INPUTS AND OUTPUTS!
  //   OUTPUT from your circuit
endmodule
